// Logisim project 2.54.circ as structural Verilog: 1 circuit, main circuit main
module main (
  input  in_1,
  input  in_2,
  input  in_3,
  input  in_4,
  input  in_5,
  input  in_6,
  output out_7,
  output out_8,
  output out_9,
  output out_10
);

  wire [1:1] undriven;

  Multiplexer #(.select(2)) multiplexer_1 (
    .in0(in_4), .in1(in_1), .in2(in_1), .in3(in_1), .out(out_7), .sel({undriven[1], in_6}), .en(in_5));
  Multiplexer #(.select(2)) multiplexer_2 (
    .in0(in_4), .in1(in_1), .in2(in_1), .in3(in_1), .out(out_8), .sel({undriven[1], in_6}), .en(in_5));
  Multiplexer #(.select(2)) multiplexer_3 (
    .in0(in_4), .in1(in_1), .in2(in_1), .in3(in_1), .out(out_9), .sel({undriven[1], in_6}), .en(in_5));
  Multiplexer #(.select(2)) multiplexer_4 (
    .in0(in_4), .in1(in_1), .in2(in_1), .in3(in_1), .out(out_10), .sel({undriven[1], in_6}), .en(in_5));
  // Pins of 1 and 2 bits meet at {undriven[1], in_6}

  assign in_2 = in_1;
  assign in_3 = in_1;
endmodule
